# Fritzing sketch schaltplan_vorlage (saved by Fritzing 0.9.5d)
breadboards: 1

parts:
  Raspberry_Pi_1 = Raspberry Pi 3 [part_number=RPI-3-V1.2]
  LED1 = smd LED [color="Red (633nm)" package="0805 [SMD]"]
  LED2 = smd LED [color="Red (633nm)" package="0805 [SMD]"]
  R1 = Resistor [tolerance=±5% resistance=220 package="0603 [SMD]"]
  R2 = Resistor [tolerance=±5% resistance=220 package="0603 [SMD]"]
  HC-SR04_Sensor_1 = HC-SR04 Ultrasonic Distance Sensor
  R3 = Resistor [tolerance=±5% resistance=220 package="0603 [SMD]"]
  R4 = Resistor [tolerance=±5% resistance=220 package="0603 [SMD]"]
  Bauteil1 = Triple Axis Magnetometer - HMC5883 Breakout
  Bauteil2 = InvenSense MPU6050

nets:
  VCC: Raspberry_Pi_1.3v3, Bauteil1.VCC, Bauteil2.VCC
  N1: Raspberry_Pi_1.GPIO2, Bauteil1.SDA, Bauteil2.SDA
  N2: Raspberry_Pi_1.GPIO3, Bauteil1.SCL, Bauteil2.SCL
  N3: Raspberry_Pi_1.GIPO27, R3.Pin_1, R4.Pin_0
  N4: Raspberry_Pi_1.GIPO13, HC-SR04_Sensor_1.TRIG
  N5: Raspberry_Pi_1.GIPO7, R2.Pin_1
  N6: Raspberry_Pi_1.GIPO8, R1.Pin_1
  GND: Raspberry_Pi_1.GND, HC-SR04_Sensor_1.GND, R4.Pin_1, Bauteil1.GND, Bauteil2.GND
  5V: Raspberry_Pi_1.5V, HC-SR04_Sensor_1.VCC
  N7: LED1.anode, R1.Pin_0
  N8: LED2.anode, R2.Pin_0
  N9: HC-SR04_Sensor_1.ECHO, R3.Pin_0
